// Logisim project 21012022059.circ as structural Verilog: 1 circuit, main circuit main
module main (
  input  CIN,
  input  _1_s_Comp,
  input  [3:0] A,
  input  Reset_A,
  input  [3:0] B,
  input  Reset_B,
  output S0,
  output S1,
  output S2,
  output S3,
  output COUT
);

  wire adder_1_cout, adder_2_cout, adder_3_cout, clock_1_out, xor_1_out, xor_2_out, xor_3_out, xor_4_out;
  wire [3:0] register_1_q, register_2_q;

  Register #(.width(4)) register_1 (.D(A), .Q(register_1_q), .clk(clock_1_out), .clr(Reset_A));  // open: en
  Register #(.width(4)) register_2 (.D(B), .Q(register_2_q), .clk(clock_1_out), .clr(Reset_B));  // open: en
  Clock clock_1 (.out(clock_1_out));
  xor xor_1 (xor_1_out, _1_s_Comp, register_2_q[0]);
  xor xor_2 (xor_2_out, _1_s_Comp, register_2_q[1]);
  xor xor_3 (xor_3_out, _1_s_Comp, register_2_q[2]);
  xor xor_4 (xor_4_out, _1_s_Comp, register_2_q[3]);
  Adder #(.width(1)) adder_1 (.a(register_1_q[0]), .b(xor_1_out), .out(S0), .cin(CIN), .cout(adder_1_cout));
  Adder #(.width(1)) adder_2 (.a(register_1_q[1]), .b(xor_2_out), .out(S1), .cin(adder_1_cout), .cout(adder_2_cout));
  Adder #(.width(1)) adder_3 (.a(register_1_q[2]), .b(xor_3_out), .out(S2), .cin(adder_2_cout), .cout(adder_3_cout));
  Adder #(.width(1)) adder_4 (.a(register_1_q[3]), .b(xor_4_out), .out(S3), .cin(adder_3_cout), .cout(COUT));

  // Notes on the sheet:
  //   Clock
  //   Umang Vyas
  //   21012022059
endmodule
